# Fritzing sketch sketch (saved by Fritzing 0.9.3b)
breadboards: 1

parts:
  KY-4 = Keyes Relay [package=THT]
  KY-5 = Keyes Relay [package=THT]
  U1 = Voltage Regulator - 5V [package="TO220 [THT]"]
  Power_plug1 = Power plug
  Part1 = Arduino Pro Mini (5V)
  Q1 = NPN-Transistor [package="TO92 [THT]"]
  M1 = DC Motor
  R1 = Resistor [tolerance=±5% resistance=220 package=THT]
  D1 = Rectifier Diode [part_number=1N4001 package="300 mil [THT]"]  # not connected

nets:
  N1: KY-4.signal, Part1.D8
  N2: KY-4.power, KY-5.power, U1.output_voltage, Part1.VCC
  N3: KY-4.ground, KY-5.ground
  N4: KY-4.NC, KY-4.NO, M1.pin_2
  N5: KY-4.C, U1.input_voltage, Power_plug1.VCC
  N6: KY-5.signal, Part1.D7
  N7: KY-5.NC, KY-5.NO, M1.pin_1
  N8: KY-5.C, Q1.C
  GND: U1.GND, Power_plug1.GND, Part1.GND, Q1.E
  N9: Part1.D9, R1.Pin_1
  N10: Q1.B, R1.Pin_0

notes:
  DC motor courtain
  12 V power supply
  l7805cv

custom parts:
  Keyes Relay: The Keyes 5V relay module is suitable for SCM development, home appliance control. It uses a 5V~12V TIL control signal which can control DC / AC signal.
